// Logisim project CUPU.circ as structural Verilog
module regs (
  input  [7:0] s0_sel,
  input  [7:0] s1_sel,
  input  [7:0] dest_sel,
  input  [31:0] data,
  input  load,
  output [31:0] out_6,
  output [31:0] out_7
);

  wire decoder_1_out0, decoder_1_out1, decoder_1_out2, decoder_1_out3, decoder_1_out4, decoder_1_out5,
       decoder_1_out6, decoder_1_out7, decoder_1_out8, decoder_1_out9, decoder_1_out10, decoder_1_out11,
       decoder_1_out12, decoder_1_out13, decoder_1_out14, decoder_1_out15, delay_1_out_2;
  wire [3:0] bit_extender_1_out, bit_extender_2_out, bit_extender_3_out;
  wire [31:0] register_1_q, register_2_q, register_3_q, register_4_q, register_5_q, register_6_q,
       register_7_q, register_8_q, register_9_q, register_10_q, register_11_q, register_12_q, register_13_q,
       register_14_q, register_15_q, register_16_q;

  Bit_Extender #(.out_width(4)) bit_extender_1 (.in(s0_sel), .out(bit_extender_1_out));
  Bit_Extender #(.out_width(4)) bit_extender_2 (.in(s1_sel), .out(bit_extender_2_out));
  Bit_Extender #(.out_width(4)) bit_extender_3 (.in(dest_sel), .out(bit_extender_3_out));
  Decoder #(.select(4)) decoder_1 (
    .out0(decoder_1_out0), .out1(decoder_1_out1), .out2(decoder_1_out2), .out3(decoder_1_out3),
    .out4(decoder_1_out4), .out5(decoder_1_out5), .out6(decoder_1_out6), .out7(decoder_1_out7),
    .out8(decoder_1_out8), .out9(decoder_1_out9), .out10(decoder_1_out10), .out11(decoder_1_out11),
    .out12(decoder_1_out12), .out13(decoder_1_out13), .out14(decoder_1_out14), .out15(decoder_1_out15),
    .sel(bit_extender_3_out), .en(delay_1_out_2));
  delay delay_1 (.in_1(load), .out_2(delay_1_out_2));
  Register #(.width(32)) register_1 (.D(data), .Q(register_1_q), .clk(decoder_1_out0));  // open: en, clr
  Register #(.width(32)) register_2 (.D(data), .Q(register_2_q), .clk(decoder_1_out1));  // open: en, clr
  Register #(.width(32)) register_3 (.D(data), .Q(register_3_q), .clk(decoder_1_out2));  // open: en, clr
  Register #(.width(32)) register_4 (.D(data), .Q(register_4_q), .clk(decoder_1_out3));  // open: en, clr
  Register #(.width(32)) register_5 (.D(data), .Q(register_5_q), .clk(decoder_1_out4));  // open: en, clr
  Register #(.width(32)) register_6 (.D(data), .Q(register_6_q), .clk(decoder_1_out5));  // open: en, clr
  Register #(.width(32)) register_7 (.D(data), .Q(register_7_q), .clk(decoder_1_out6));  // open: en, clr
  Register #(.width(32)) register_8 (.D(data), .Q(register_8_q), .clk(decoder_1_out7));  // open: en, clr
  Register #(.width(32)) register_9 (.D(data), .Q(register_9_q), .clk(decoder_1_out8));  // open: en, clr
  Register #(.width(32)) register_10 (.D(data), .Q(register_10_q), .clk(decoder_1_out9));  // open: en, clr
  Register #(.width(32)) register_11 (.D(data), .Q(register_11_q), .clk(decoder_1_out10));  // open: en, clr
  Register #(.width(32)) register_12 (.D(data), .Q(register_12_q), .clk(decoder_1_out11));  // open: en, clr
  Register #(.width(32)) register_13 (.D(data), .Q(register_13_q), .clk(decoder_1_out12));  // open: en, clr
  Register #(.width(32)) register_14 (.D(data), .Q(register_14_q), .clk(decoder_1_out13));  // open: en, clr
  Register #(.width(32)) register_15 (.D(data), .Q(register_15_q), .clk(decoder_1_out14));  // open: en, clr
  Register #(.width(32)) register_16 (.D(data), .Q(register_16_q), .clk(decoder_1_out15));  // open: en, clr
  Multiplexer #(.select(4), .width(32)) multiplexer_1 (
    .in0(register_1_q), .in1(register_2_q), .in2(register_3_q), .in3(register_4_q), .in4(register_5_q),
    .in5(register_6_q), .in6(register_7_q), .in7(register_8_q), .in8(register_9_q), .in9(register_10_q),
    .in10(register_11_q), .in11(register_12_q), .in12(register_13_q), .in13(register_14_q),
    .in14(register_15_q), .in15(register_16_q), .out(out_6), .sel(bit_extender_1_out));
  Multiplexer #(.select(4), .width(32)) multiplexer_2 (
    .in0(register_1_q), .in1(register_2_q), .in2(register_3_q), .in3(register_4_q), .in4(register_5_q),
    .in5(register_6_q), .in6(register_7_q), .in7(register_8_q), .in8(register_9_q), .in9(register_10_q),
    .in10(register_11_q), .in11(register_12_q), .in12(register_13_q), .in13(register_14_q),
    .in14(register_15_q), .in15(register_16_q), .out(out_7), .sel(bit_extender_2_out));
endmodule

module delay (
  input  in_1,
  output out_2
);

  wire buffer_1_out, buffer_2_out, buffer_3_out, buffer_4_out, buffer_5_out, buffer_6_out, buffer_7_out,
       buffer_8_out, buffer_9_out, buffer_10_out, buffer_11_out, buffer_12_out, buffer_13_out, buffer_14_out,
       buffer_15_out, buffer_16_out, buffer_17_out, buffer_18_out, buffer_19_out, buffer_20_out,
       buffer_21_out, buffer_22_out, buffer_23_out, buffer_24_out, buffer_25_out, buffer_26_out,
       buffer_27_out, buffer_28_out, buffer_29_out, buffer_30_out, buffer_31_out, buffer_32_out,
       buffer_33_out, buffer_34_out, buffer_35_out, buffer_36_out, buffer_37_out, buffer_38_out,
       buffer_39_out, buffer_40_out, buffer_41_out, buffer_42_out, buffer_43_out, buffer_44_out,
       buffer_45_out, buffer_46_out, buffer_47_out;

  buf buffer_1 (buffer_1_out, in_1);
  buf buffer_2 (buffer_2_out, buffer_1_out);
  buf buffer_3 (buffer_3_out, buffer_2_out);
  buf buffer_4 (buffer_4_out, buffer_5_out);
  buf buffer_5 (buffer_5_out, buffer_6_out);
  buf buffer_6 (buffer_6_out, buffer_7_out);
  buf buffer_7 (buffer_7_out, buffer_15_out);
  buf buffer_8 (buffer_8_out, buffer_4_out);
  buf buffer_9 (buffer_9_out, buffer_8_out);
  buf buffer_10 (buffer_10_out, buffer_9_out);
  buf buffer_11 (buffer_11_out, buffer_3_out);
  buf buffer_12 (buffer_12_out, buffer_11_out);
  buf buffer_13 (buffer_13_out, buffer_12_out);
  buf buffer_14 (buffer_14_out, buffer_13_out);
  buf buffer_15 (buffer_15_out, buffer_16_out);
  buf buffer_16 (buffer_16_out, buffer_17_out);
  buf buffer_17 (buffer_17_out, buffer_18_out);
  buf buffer_18 (buffer_18_out, buffer_27_out);
  buf buffer_19 (buffer_19_out, buffer_10_out);
  buf buffer_20 (buffer_20_out, buffer_19_out);
  buf buffer_21 (buffer_21_out, buffer_20_out);
  buf buffer_22 (buffer_22_out, buffer_21_out);
  buf buffer_23 (buffer_23_out, buffer_14_out);
  buf buffer_24 (buffer_24_out, buffer_23_out);
  buf buffer_25 (buffer_25_out, buffer_24_out);
  buf buffer_26 (buffer_26_out, buffer_25_out);
  buf buffer_27 (buffer_27_out, buffer_28_out);
  buf buffer_28 (buffer_28_out, buffer_29_out);
  buf buffer_29 (buffer_29_out, buffer_30_out);
  buf buffer_30 (buffer_30_out, buffer_39_out);
  buf buffer_31 (buffer_31_out, buffer_22_out);
  buf buffer_32 (buffer_32_out, buffer_31_out);
  buf buffer_33 (buffer_33_out, buffer_32_out);
  buf buffer_34 (buffer_34_out, buffer_33_out);
  buf buffer_35 (buffer_35_out, buffer_26_out);
  buf buffer_36 (buffer_36_out, buffer_35_out);
  buf buffer_37 (buffer_37_out, buffer_36_out);
  buf buffer_38 (buffer_38_out, buffer_37_out);
  buf buffer_39 (buffer_39_out, buffer_40_out);
  buf buffer_40 (buffer_40_out, buffer_41_out);
  buf buffer_41 (buffer_41_out, buffer_42_out);
  buf buffer_42 (buffer_42_out, buffer_47_out);
  buf buffer_43 (buffer_43_out, buffer_34_out);
  buf buffer_44 (buffer_44_out, buffer_43_out);
  buf buffer_45 (buffer_45_out, buffer_44_out);
  buf buffer_46 (buffer_46_out, buffer_45_out);
  buf buffer_47 (buffer_47_out, buffer_38_out);
  buf buffer_48 (out_2, buffer_46_out);
endmodule

module cpu (
  input  [7:0] in_1,
  output [7:0] out_2,
  output [31:0] out_3,
  output out_4
);

  wire decoder_1_out8, decoder_1_out9, decoder_1_out10, decoder_1_out11, decoder_1_out12, decoder_1_out13,
       decoder_1_out14, decoder_1_out15, undriven;
  wire [7:0] dest_q, inst_q, register_1_q, register_3_q, register_4_q, register_5_q, register_6_q, s0_q, s1_q;
  wire [31:0] multiplexer_2_out, register_2_q, regs_1_out_6;

  Decoder #(.select(4)) decoder_1 (
    .out8(decoder_1_out8), .out9(decoder_1_out9), .out10(decoder_1_out10), .out11(decoder_1_out11),
    .out12(decoder_1_out12), .out13(decoder_1_out13), .out14(decoder_1_out14), .out15(decoder_1_out15));  // open: out0, out1, out2, out3, out4, out5, out6, out7, sel, en
  Register register_1 (.D(in_1), .Q(register_1_q));  // open: en, clk, clr
  Register inst (.D(in_1), .Q(inst_q), .clk(decoder_1_out8));  // open: en, clr
  Register #(.width(32)) address (.D(multiplexer_2_out));  // open: en, Q, clk, clr
  Register s0 (.D(in_1), .Q(s0_q), .clk(decoder_1_out9));  // open: en, clr
  Register #(.width(32)) register_2 (.D(multiplexer_2_out), .Q(register_2_q));  // open: en, clk, clr
  Register s1 (.D(in_1), .Q(s1_q), .clk(decoder_1_out10));  // open: en, clr
  Multiplexer #(.select(2), .width(8)) multiplexer_1 (
    .in0(register_2_q[31:24]), .in1(register_2_q[23:16]), .in2(register_2_q[15:8]), .in3(register_2_q[7:0]));  // open: out, sel
  Register dest (.D(in_1), .Q(dest_q), .clk(decoder_1_out11));  // open: en, clr
  Register register_3 (.D(in_1), .Q(register_3_q), .clk(decoder_1_out15), .clr(undriven));  // open: en
  Register register_4 (.D(in_1), .Q(register_4_q), .clk(decoder_1_out14), .clr(undriven));  // open: en
  Register register_5 (.D(in_1), .Q(register_5_q), .clk(decoder_1_out13), .clr(undriven));  // open: en
  Multiplexer #(.select(3), .width(32)) multiplexer_2 (
    .in0({register_3_q, register_4_q, register_5_q, register_6_q}), .in1(regs_1_out_6),
    .out(multiplexer_2_out));  // open: in2, in3, in4, in5, in6, in7, sel
  regs regs_1 (
    .s0_sel(s0_q), .s1_sel(s1_q), .dest_sel(dest_q), .data(multiplexer_2_out), .out_6(regs_1_out_6));  // open: load, out_7
  Register register_6 (.D(in_1), .Q(register_6_q), .clk(decoder_1_out12), .clr(undriven));  // open: en
endmodule
